# Fritzing sketch Fritzing (saved by Fritzing 0.8.7b)
circuit board: 8.46667cm x 5.64444cm
breadboards: 1

parts:
  U1 = NodeMCU V1.0
  KY-1 = Keyes Relay [package=THT]
  Part2 = Lilypad Battery Connect
  L1 = Solenoid
  S1 = Momentary Switch [package=ksa_sealed_tac_switch]
  LED1 = LED - 5mm [color="Red (633nm)" package="5 mm [THT]"]

nets (from the schematic view):
  N1: U1.D1, KY-1.ground, LED1.cathode
  N2: U1.GND, KY-1.power, LED1.anode
  N3: U1.Vin, KY-1.signal
  N4: U1.SD3, S1.3
  N5: KY-1.C, Part2.+
  N6: KY-1.NO, L1.pin2
  N7: Part2.-, L1.pin1

notes:
  IN
  GND
  VCC
  12V DC power supply

custom parts:
  NodeMCU V1.0: ESP9266 based NodeMCU
  Keyes Relay: The Keyes 5V relay module is suitable for SCM development, home appliance control. It uses a 5V~12V TIL control signal which can control DC / AC signal.
